// Logisim project 1_Uebung.circ as structural Verilog: 2 circuits, main circuit Aufgabe2
module Aufgabe2 (
  input  A,
  input  B,
  input  C,
  input  D,
  input  E,
  input  F,
  output Y
);

  wire nand_1_out, nand_2_out, nand_3_out, nand_4_out, not_1_out, not_2_out, not_3_out;

  not not_1 (not_1_out, A);
  not not_2 (not_2_out, E);
  nand nand_1 (nand_1_out, B, C);
  nand nand_2 (nand_2_out, not_2_out, F);
  not not_3 (not_3_out, nand_2_out);
  nand nand_3 (nand_3_out, not_1_out, nand_1_out);
  nand nand_4 (nand_4_out, D, not_3_out);
  nand nand_5 (Y, nand_3_out, nand_4_out);
endmodule

module Aufgabe3 (
  input  A,
  input  B,
  input  C,
  output Y
);

  wire transistor_1_out, transistor_3_out, transistor_5_out;

  Transistor transistor_1 (.in(1'b1), .out(transistor_1_out), .gate(A));
  Transistor #(.\type ("n")) transistor_2 (.in(1'b0), .out(transistor_1_out), .gate(A));
  Transistor transistor_3 (.in(1'b1), .out(transistor_3_out), .gate(transistor_1_out));
  Transistor #(.\type ("n")) transistor_4 (.in(transistor_5_out), .out(Y), .gate(transistor_1_out));
  Transistor #(.\type ("n")) transistor_5 (.in(1'b0), .out(transistor_5_out), .gate(B));
  Transistor transistor_6 (.in(1'b1), .out(transistor_3_out), .gate(B));
  Transistor transistor_7 (.in(transistor_3_out), .out(Y), .gate(C));
  Transistor #(.\type ("n")) transistor_8 (.in(1'b0), .out(Y), .gate(C));
endmodule
