// Logisim project Versuch1.circ as structural Verilog: 6 circuits, main circuit main
module main (
  input  X0,
  input  X1,
  output out_3
);

  NAND_NMOS nand_nmos_1 (.X1(X0), .X2(X1), .Y(out_3));

  // Notes on the sheet:
  //   Nils Helming
  //   Nabeel Elamaireh
  //   Lukas Piening
  //   27.10.2020
endmodule

module NAND_NMOS (
  input  X1,
  input  X2,
  output Y
);

  wire transistor_2_out;

  Pull_Resistor #(.pull(1)) pull_resistor_1 (.node(Y));
  Transistor #(.\type ("n")) transistor_1 (.in(transistor_2_out), .out(Y), .gate(X1));
  Transistor #(.\type ("n")) transistor_2 (.in(1'b0), .out(transistor_2_out), .gate(X2));

  // Notes on the sheet:
  //   Nils Helming
  //   Nabeel Elamaireh
  //   Lukas Piening
  //   27.10.2020
endmodule

module NAND_CMOS (
  input  X1,
  input  X2,
  output f
);

  wire transistor_4_out;

  Transistor transistor_1 (.in(1'b1), .out(f), .gate(X1));
  Transistor transistor_2 (.in(1'b1), .out(f), .gate(X2));
  Transistor #(.\type ("n")) transistor_3 (.in(transistor_4_out), .out(f), .gate(X1));
  Transistor #(.\type ("n")) transistor_4 (.in(1'b0), .out(transistor_4_out), .gate(X2));

  // Notes on the sheet:
  //   Nils Helming
  //   Nabeel Elamaireh
  //   Lukas Piening
  //   27.10.2020
endmodule

module NOR_CMOS (
  input  X1,
  input  X2,
  output Y
);

  wire transistor_2_out;

  Transistor #(.\type ("n")) transistor_1 (.in(1'b0), .out(Y), .gate(X1));
  Transistor transistor_2 (.in(1'b1), .out(transistor_2_out), .gate(X1));
  Transistor transistor_3 (.in(transistor_2_out), .out(Y), .gate(X2));
  Transistor #(.\type ("n")) transistor_4 (.in(1'b0), .out(Y), .gate(X2));

  // Notes on the sheet:
  //   Nils Helming
  //   Nabeel Elamaireh
  //   Lukas Piening
  //   27.10.2020
endmodule

module INV_CMOS (
  input  X1,
  output Y
);

  Transistor transistor_1 (.in(1'b1), .out(Y), .gate(X1));
  Transistor #(.\type ("n")) transistor_2 (.in(1'b0), .out(Y), .gate(X1));

  // Notes on the sheet:
  //   Nils Helming
  //   Nabeel Elamaireh
  //   Lukas Piening
  //   27.10.2020
endmodule

module XOR_CMOS (
  input  X1,
  input  X2,
  output Y
);

  wire inv_cmos_1_y, inv_cmos_2_y, nand_cmos_1_f, nand_cmos_2_f;

  INV_CMOS inv_cmos_1 (.X1(X1), .Y(inv_cmos_1_y));
  INV_CMOS inv_cmos_2 (.X1(X2), .Y(inv_cmos_2_y));
  NAND_CMOS nand_cmos_1 (.X1(inv_cmos_1_y), .X2(X2), .f(nand_cmos_1_f));
  NAND_CMOS nand_cmos_2 (.X1(X1), .X2(inv_cmos_2_y), .f(nand_cmos_2_f));
  NAND_CMOS nand_cmos_3 (.X1(nand_cmos_1_f), .X2(nand_cmos_2_f), .f(Y));

  // Notes on the sheet:
  //   Nils Helming
  //   Nabeel Elamaireh
  //   Lukas Piening
  //   27.10.2020
endmodule
