// Logisim project Zusatz.circ as structural Verilog: 2 circuits, main circuit Logic
module Logic (
  input  A,
  input  B,
  input  C,
  input  D,
  output Y
);

  wire nand_1_out, nand_2_out, nand_3_out, not_1_out, not_2_out, not_3_out;

  not not_1 (not_1_out, B);
  not not_2 (not_2_out, C);
  not not_3 (not_3_out, D);
  nand nand_1 (nand_1_out, not_1_out, D);
  nand nand_2 (nand_2_out, A, C, not_3_out);
  nand nand_3 (nand_3_out, A, not_2_out, D);
  nand nand_4 (Y, nand_1_out, nand_2_out, nand_3_out);
endmodule

module Bausteine (
  input  A,
  input  B,
  input  C,
  input  D,
  output Y
);

  wire n7404_1_pin2, n7404_1_pin4, n7404_1_pin6, n7410_1_pin6, n7410_1_pin8, n7410_1_pin12;

  _7404 u_7404_1 (
    .pin1(B), .pin2(n7404_1_pin2), .pin3(C), .pin4(n7404_1_pin4), .pin5(D), .pin6(n7404_1_pin6));  // open: pin13, pin12, pin11, pin10, pin9, pin8
  _7410 u_7410_1 (
    .pin1(n7404_1_pin2), .pin2(n7404_1_pin2), .pin3(A), .pin4(C), .pin5(n7404_1_pin6), .pin6(n7410_1_pin6),
    .pin13(D), .pin12(n7410_1_pin12), .pin11(D), .pin10(n7404_1_pin4), .pin9(A), .pin8(n7410_1_pin8));
  _7410 u_7410_2 (
    .pin1(n7410_1_pin12), .pin2(n7410_1_pin6), .pin13(n7410_1_pin8), .pin12(Y));  // open: pin3, pin4, pin5, pin6, pin11, pin10, pin9, pin8
endmodule
