// Logisim project Versuch2.circ as structural Verilog: 2 circuits, main circuit DisjunktiveMinimalform
module DisjunktiveMinimalform (
  input  X3,
  input  X2,
  input  X1,
  input  X0,
  output Y
);

  wire nand_1_out, nand_2_out, nand_3_out, not_1_out, not_2_out;

  not not_1 (not_1_out, X1);
  not not_2 (not_2_out, X0);
  nand nand_1 (nand_1_out, X3, X2);
  nand nand_2 (nand_2_out, not_1_out, not_2_out);
  nand nand_3 (nand_3_out, X3, not_2_out);
  nand nand_4 (Y, nand_1_out, nand_2_out, nand_3_out);

  // Notes on the sheet:
  //   Nils Helming
  //   Nabeel Elamaireh
  //   Lukas Piening
  //   17.11.2020
endmodule

module KonjunktiveMinimalform (
  input  X3,
  input  X2,
  input  X1,
  input  X0,
  output Y
);

  wire nand_1_out, nand_2_out, nand_3_out, nand_4_out, not_1_out, not_2_out;

  not not_1 (not_1_out, X3);
  not not_2 (not_2_out, X2);
  nand nand_1 (nand_1_out, not_1_out, X1);
  nand nand_2 (nand_2_out, not_1_out, X0);
  nand nand_3 (nand_3_out, not_2_out, X0);
  not not_3 (Y, nand_4_out);
  nand nand_4 (nand_4_out, nand_1_out, nand_2_out, nand_3_out);

  // Notes on the sheet:
  //   Nils Helming
  //   Nabeel Elamaireh
  //   Lukas Piening
  //   17.11.2020
endmodule
