// Logisim project Aufgabe3.circ as structural Verilog: 3 circuits, main circuit VA1
module VA1 (
  input  a,
  input  b,
  input  c,
  output s1,
  output s0
);

  wire nand_1_out, nand_2_out, nand_3_out, xor_1_out;

  xor xor_1 (xor_1_out, a, b);
  nand nand_1 (nand_1_out, a, b);
  nand nand_2 (nand_2_out, a, c);
  nand nand_3 (nand_3_out, b, c);
  xor xor_2 (s0, xor_1_out, c);
  nand nand_4 (s1, nand_1_out, nand_2_out, nand_3_out);

  // Notes on the sheet:
  //   Nils Helming
  //   01.12.2020
endmodule

module VA2 (
  input  a,
  input  b,
  input  c,
  output s1,
  output s0
);

  wire n7400_1_pin3, n7400_1_pin6, n7400_1_pin11, n7486_1_pin3;

  _7400 #(.ShowInternalStructure("true")) u_7400_1 (
    .pin1(a), .pin2(b), .pin3(n7400_1_pin3), .pin4(b), .pin5(c), .pin6(n7400_1_pin6), .pin13(a), .pin12(c),
    .pin11(n7400_1_pin11));  // open: pin10, pin9, pin8
  _7486 #(.ShowInternalStructure("true")) u_7486_1 (
    .pin1(a), .pin2(b), .pin3(n7486_1_pin3), .pin4(n7486_1_pin3), .pin5(c), .pin6(s0));  // open: pin13, pin12, pin11, pin10, pin9, pin8
  _7410 #(.ShowInternalStructure("true")) u_7410_1 (
    .pin1(n7400_1_pin3), .pin2(n7400_1_pin6), .pin13(n7400_1_pin11), .pin12(s1));  // open: pin3, pin4, pin5, pin6, pin11, pin10, pin9, pin8

  // Notes on the sheet:
  //   Nils Helming
  //   01.12.2020
endmodule

module Anzeige (
  input  [3:0] value
);

  wire [6:0] encoder_data;

  ROM #(.addrWidth(4), .dataWidth(7)) encoder (.addr(value), .data(encoder_data));
  _7_Segment_Display sseg (
    .g(encoder_data[6]), .f(encoder_data[5]), .a(encoder_data[0]), .b(encoder_data[1]), .e(encoder_data[4]),
    .d(encoder_data[3]), .c(encoder_data[2]));  // open: dp

  // Notes on the sheet:
  //   Nils Helming
  //   01.12.2020
  //   contents of encoder (hex, n*v repeats v):
  //   3f 6 5b 4f 66 6d 7d 7 7f 6f 77 7c 39 5e 79 71
endmodule
