// Logisim project Aufgabe5.circ as structural Verilog: 2 circuits, main circuit Zaehler
module Zaehler (
  input  CLK,
  output TC
);

  wire and_1_out, and_2_out, and_4_out, t_ff_1_q, t_ff_1_qn, t_ff_2_q, t_ff_2_qn, t_ff_3_q, t_ff_3_qn,
       t_ff_4_qn;

  T_Flip_Flop t_ff_1 (.T(1'b1), .clk(CLK), .Q(t_ff_1_q), .Qn(t_ff_1_qn));  // open: reset, preset
  and and_1 (and_1_out, 1'b1, t_ff_1_q);
  T_Flip_Flop t_ff_2 (.T(and_1_out), .clk(CLK), .Q(t_ff_2_q), .Qn(t_ff_2_qn));  // open: reset, preset
  and and_2 (and_2_out, and_1_out, t_ff_2_q);
  T_Flip_Flop t_ff_3 (.T(and_2_out), .clk(CLK), .Q(t_ff_3_q), .Qn(t_ff_3_qn));  // open: reset, preset
  and and_3 (TC, t_ff_1_qn, t_ff_2_qn, t_ff_3_qn, t_ff_4_qn);
  and and_4 (and_4_out, and_2_out, t_ff_3_q);
  T_Flip_Flop t_ff_4 (.T(and_4_out), .clk(CLK), .Qn(t_ff_4_qn));  // open: Q, reset, preset

  // Notes on the sheet:
  //   Nils Helming
  //   Nabeel Elamaireh
  //   Lukas Piening
  //   05.01.2021
endmodule

module Ampel (
);

  wire and_1_out, and_2_out, and_3_out, and_4_out, CLK_out, CTR_tc, not_1_out, or_1_out, xor_1_out, Z0_q,
       Z1_q;

  Clock CLK (.out(CLK_out));
  D_Flip_Flop Z1 (.D(or_1_out), .clk(CLK_out), .Q(Z1_q));  // open: Qn, preset, reset
  D_Flip_Flop Z0 (.D(xor_1_out), .clk(CLK_out), .Q(Z0_q));  // open: Qn, preset, reset
  xor xor_1 (xor_1_out, Z0_q, CTR_tc);
  and and_1 (and_1_out, Z0_q, ~Z1_q, CTR_tc);  // AND_Gate
  or or_1 (or_1_out, and_1_out, and_2_out, and_3_out);
  and and_2 (and_2_out, Z1_q, ~Z0_q);  // AND_Gate
  and and_3 (and_3_out, Z1_q, ~CTR_tc);  // AND_Gate
  Zaehler CTR (.CLK(CLK_out), .TC(CTR_tc));
  not not_1 (not_1_out, Z1_q);
  and and_4 (and_4_out, Z1_q, ~Z0_q);  // AND_Gate
  LED ROT (.in(not_1_out));
  LED GELB (.in(Z0_q));
  LED GRUEN (.in(and_4_out));

  // Notes on the sheet:
  //   Nils Helming
  //   Nabeel Elamaireh
  //   Lukas Piening
  //   05.01.2021
  //   Z1*
  //   Z0*
  //   Z1
  //   TC
  //   Z0
  //   Z1
  //   TC
  //   Z0
endmodule
